// Digital circuit D_front_montant.dig as structural Verilog
module D_front_montant (
  input  Clk,
  input  D,
  output Q,
  output Q_2,
  output R,
  output S
);

  wire nand_1_out, nand_4_out;

  nand nand_1 (nand_1_out, nand_4_out, S);
  nand nand_2 (S, nand_1_out, Clk);
  nand nand_3 (R, S, Clk, nand_4_out);
  nand nand_4 (nand_4_out, R, D);
  nand nand_5 (Q, S, Q_2);
  nand nand_6 (Q_2, Q, R);
endmodule
