// Digital circuit D_mast_slave.dig as structural Verilog
module D_mast_slave (
  input  D,
  input  Clk,
  output Q
);

  wire d_ff_1_q, not_1_out;

  D_FF d_ff_1 (.D(D), .C(Clk), .Q(d_ff_1_q));  // open: nQ
  not not_1 (not_1_out, Clk);
  D_FF d_ff_2 (.D(d_ff_1_q), .C(not_1_out), .Q(Q));  // open: nQ
endmodule
