// Digital circuit SRlatch_nand_en.dig as structural Verilog
module SRlatch_nand_en (
  input  R,
  input  S,
  input  E,
  output Q,
  output Q_2
);

  wire nand_1_out, nand_2_out;

  nand nand_1 (nand_1_out, S, E);
  nand nand_2 (nand_2_out, E, R);
  nand nand_3 (Q, nand_1_out, Q_2);
  nand nand_4 (Q_2, Q, nand_2_out);
endmodule
