// Digital circuit add_sous_deb.dig as structural Verilog
module add_sous_deb (
  input  b_0,
  input  a_0,
  input  a_1,
  input  a_2,
  input  a_3,
  input  b_1,
  input  b_2,
  input  b_3,
  input  O,
  output S_0,
  output S_1,
  output S_2,
  output S_3,
  output R_4,
  output D
);

  wire fulladderxor_2_r_i, fulladderxor_3_r_i, fulladderxor_4_r_i, xor_1_out, xor_3_out, xor_4_out, xor_5_out;

  xor xor_1 (xor_1_out, b_3, O);
  fulladderxor fulladderxor_1 (.a_i(a_3), .b_i(xor_1_out), .r_i_1(fulladderxor_2_r_i), .S_i(S_3), .R_i(R_4));
  xor xor_2 (D, fulladderxor_2_r_i, R_4);
  xor xor_3 (xor_3_out, b_2, O);
  fulladderxor fulladderxor_2 (
    .a_i(a_2), .b_i(xor_3_out), .r_i_1(fulladderxor_3_r_i), .S_i(S_2), .R_i(fulladderxor_2_r_i));
  xor xor_4 (xor_4_out, b_1, O);
  fulladderxor fulladderxor_3 (
    .a_i(a_1), .b_i(xor_4_out), .r_i_1(fulladderxor_4_r_i), .S_i(S_1), .R_i(fulladderxor_3_r_i));
  xor xor_5 (xor_5_out, b_0, O);
  fulladderxor fulladderxor_4 (.a_i(a_0), .b_i(xor_5_out), .r_i_1(O), .S_i(S_0), .R_i(fulladderxor_4_r_i));
endmodule
