// Digital circuit basculeT.dig as structural Verilog
module basculeT (
  input  T,
  input  T_2
);

  wire d_ff_1_q, jk_ff_1_q, xor_1_out;

  xor xor_1 (xor_1_out, d_ff_1_q, T_2);
  JK_FF jk_ff_1 (.J(T), .K(T), .Q(jk_ff_1_q));  // open: C, nQ
  D_FF d_ff_1 (.D(xor_1_out), .Q(d_ff_1_q));  // open: C, nQ
endmodule
