// Digital circuit bascule_JK.dig as structural Verilog
module bascule_JK (
  input  J,
  input  K,
  input  clk,
  output Q,
  output Q_2
);

  wire and_1_out, and_2_out, not_1_out, or_1_out;

  not not_1 (not_1_out, K);
  and and_1 (and_1_out, Q_2, J);
  and and_2 (and_2_out, not_1_out, Q);
  or or_1 (or_1_out, and_1_out, and_2_out);
  D_FF d_ff_1 (.D(or_1_out), .C(clk), .Q(Q), .nQ(Q_2));
endmodule
