// Digital circuit buf_3s.dig as structural Verilog
module buf_3s (
  input  \Entrée ,
  input  \Contrôle ,
  output Sortie
);

  assign Sortie = \Contrôle  ? \Entrée  : 1'bz;  // Driver driver_1
endmodule
