// Digital circuit bus_trans.dig as structural Verilog
module bus_trans (
  input  I_O,
  input  E,
  output O_I
);

  wire not_1_out;

  assign O_I = E ? I_O : 1'bz;  // Driver driver_1
  assign I_O = not_1_out ? O_I : 1'bz;  // Driver driver_2
  not not_1 (not_1_out, E);
endmodule
