// Digital circuit bus_trans8.dig as structural Verilog
module bus_trans8 (
  input  [7:0] I_O,
  input  \Lecture_écriture ,
  output [7:0] O_I
);

  wire not_1_out;

  assign O_I = \Lecture_écriture  ? I_O : 8'bz;  // Driver driver_1
  assign I_O = not_1_out ? O_I : 8'bz;  // Driver driver_2
  not not_1 (not_1_out, \Lecture_écriture );
endmodule
