// Digital circuit cell_logique.dig as structural Verilog
module cell_logique (
  input  a,
  input  b,
  input  c,
  input  d,
  input  R_i,
  input  clk,
  input  H,
  input  s_1,
  input  s_2,
  output O,
  output R_o
);

  wire add_1_s, d_ff_1_q, lookuptable_1_out, lookuptable_2_out, multiplexer_1_out, multiplexer_2_out;

  LookUpTable lookuptable_1 (.in0(a), .in1(b), .in2(c), .out(lookuptable_1_out));
  LookUpTable lookuptable_2 (.in0(a), .in1(b), .in2(c), .out(lookuptable_2_out));
  Add add_1 (.a(lookuptable_1_out), .b(lookuptable_2_out), .c_i(R_i), .s(add_1_s), .c_o(R_o));
  Multiplexer multiplexer_1 (.sel(d), .in_0(lookuptable_1_out), .in_1(lookuptable_2_out), .out(multiplexer_1_out));
  Multiplexer multiplexer_2 (.sel(s_1), .in_0(add_1_s), .in_1(multiplexer_1_out), .out(multiplexer_2_out));
  D_FF d_ff_1 (.D(multiplexer_2_out), .C(clk), .Q(d_ff_1_q));  // open: nQ
  Multiplexer multiplexer_3 (.sel(s_2), .in_0(multiplexer_2_out), .in_1(d_ff_1_q), .out(O));

  assign H = clk;
endmodule
