// Digital circuit cell_ram.dig as structural Verilog
module cell_ram (
  input  \Entrée ,
  input  \Sélect ,
  input  \Lect__Écrit ,
  output Sortie
);

  wire and_1_out, and_2_out, not_1_out, not_2_out, rs_ff_as_1_q;

  not not_1 (not_1_out, \Entrée );
  and and_1 (and_1_out, \Sélect , not_2_out, \Entrée );
  and and_2 (and_2_out, \Sélect , not_2_out, not_1_out);
  not not_2 (not_2_out, \Lect__Écrit );
  RS_FF_AS rs_ff_as_1 (.S(and_1_out), .R(and_2_out), .Q(rs_ff_as_1_q));  // open: nQ
  and and_3 (Sortie, \Sélect , rs_ff_as_1_q, \Lect__Écrit );
endmodule
