// Digital circuit cir_seq_a_analyser.dig as structural Verilog
module cir_seq_a_analyser (
  input  E,
  input  clk,
  output Qa,
  output Qb
);

  wire and_1_out, and_2_out, or_1_out, or_2_out;

  and and_1 (and_1_out, Qa, Qb);
  and and_2 (and_2_out, E, Qa);
  or or_1 (or_1_out, Qb, and_2_out);
  or or_2 (or_2_out, and_1_out, E);
  D_FF d_ff_1 (.D(or_1_out), .C(clk), .Q(Qa));  // open: nQ
  D_FF d_ff_2 (.D(or_2_out), .C(clk), .Q(Qb));  // open: nQ
endmodule
