// Digital circuit circ_altern_comp_ps1.dig as structural Verilog
module circ_altern_comp_ps1 (
  input  a,
  input  b,
  input  c,
  output Y
);

  wire not_1_out, not_2_out, not_3_out, or_1_out, or_2_out, or_3_out;

  not not_1 (not_1_out, a);
  not not_2 (not_2_out, b);
  not not_3 (not_3_out, c);
  or or_1 (or_1_out, a, not_2_out);
  or or_2 (or_2_out, not_1_out, b, c);
  or or_3 (or_3_out, not_2_out, not_3_out);
  nand nand_1 (Y, or_1_out, or_2_out, or_3_out);
endmodule
