// Digital circuit circ_altern_comp_sp1.dig as structural Verilog
module circ_altern_comp_sp1 (
  input  a,
  input  b,
  input  c,
  output Y
);

  wire and_1_out, and_2_out, and_3_out, not_1_out, not_2_out, not_3_out;

  not not_1 (not_1_out, a);
  not not_2 (not_2_out, b);
  not not_3 (not_3_out, c);
  and and_1 (and_1_out, not_1_out, not_2_out);
  and and_2 (and_2_out, a, b, not_3_out);
  and and_3 (and_3_out, not_2_out, c);
  nor nor_1 (Y, and_1_out, and_2_out, and_3_out);
endmodule
