// Digital circuit circ_altern_comp_sp2.dig as structural Verilog
module circ_altern_comp_sp2 (
  input  a,
  input  b,
  input  c,
  output Y
);

  wire nand_1_out, nand_2_out, nand_3_out, not_1_out, not_2_out, not_3_out;

  not not_1 (not_1_out, a);
  not not_2 (not_2_out, b);
  not not_3 (not_3_out, c);
  nand nand_1 (nand_1_out, not_1_out, not_2_out);
  nand nand_2 (nand_2_out, a, b, not_3_out);
  nand nand_3 (nand_3_out, not_2_out, c);
  nor nor_1 (Y, ~nand_1_out, ~nand_3_out);  // NOr open: In_2
endmodule
