// Digital circuit circ_altern_ps2.dig as structural Verilog
module circ_altern_ps2 (
  input  a,
  input  b,
  input  c,
  output Y
);

  wire nor_1_out, nor_2_out, nor_3_out, not_1_out, not_2_out, not_3_out;

  not not_1 (not_1_out, a);
  not not_2 (not_2_out, b);
  not not_3 (not_3_out, c);
  nor nor_1 (nor_1_out, a, b);
  nor nor_2 (nor_2_out, not_1_out, not_2_out, c);
  nor nor_3 (nor_3_out, b, not_3_out);
  and and_1 (Y, ~nor_1_out, ~nor_2_out, ~nor_3_out);  // And
endmodule
