// Digital circuit circuit_analyser.dig as structural Verilog
module circuit_analyser (
  input  A,
  input  B,
  input  C,
  input  D,
  output F_1,
  output I_1,
  output I_2
);

  wire not_1_out;

  not not_1 (not_1_out, A);
  and and_1 (I_1, not_1_out, B, C);
  nor nor_1 (I_2, A, D);
  and and_2 (F_1, I_1, I_2);
endmodule
