// Digital circuit circuit_inconnu2.dig as structural Verilog
module circuit_inconnu2 (
  input  A,
  input  B,
  input  C,
  input  D,
  output F1,
  output I1,
  output I2
);

  wire not_1_out;

  not not_1 (not_1_out, A);
  and and_1 (I1, not_1_out, B, C);
  nor nor_1 (I2, A, D);
  and and_2 (F1, I1, I2);
endmodule
