// Digital circuit circuit_inconnu_analyse.dig as structural Verilog
module circuit_inconnu_analyse (
  input  A,
  input  B,
  input  C,
  input  D,
  output F1,
  output I1,
  output I2,
  output I3,
  output I4,
  output I5
);

  wire not_1_out;

  not not_1 (not_1_out, D);
  nand nand_1 (I1, A, B, C, D);
  and and_1 (I2, A, not_1_out);
  or or_1 (I3, A, B);
  or or_2 (I4, I1, I3, I2);
  nor nor_1 (I5, A, A, C);
  and and_2 (F1, I4, I5);
endmodule
