// Digital circuit circuit_inconnu_simplifie.dig as structural Verilog
module circuit_inconnu_simplifie (
  input  A,
  input  C,
  output Y
);

  wire not_1_out, not_2_out;

  not not_1 (not_1_out, A);
  not not_2 (not_2_out, C);
  and and_1 (Y, not_1_out, not_2_out);
endmodule
