// Digital circuit comparateur.dig as structural Verilog
module comparateur (
  input  a_i,
  input  b_i,
  output A_lt_B,
  output A_eq_B,
  output A_gt_B
);

  wire not_1_out, not_2_out;

  not not_1 (not_1_out, a_i);
  not not_2 (not_2_out, b_i);
  and and_1 (A_lt_B, not_1_out, b_i);
  and and_2 (A_gt_B, a_i, not_2_out);
  nor nor_1 (A_eq_B, A_lt_B, A_gt_B);
endmodule
