// Digital circuit comparateur_4b.dig as structural Verilog
module comparateur_4b (
  input  a_3,
  input  b_3,
  input  a_2,
  input  b_2,
  input  a_1,
  input  b_1,
  input  a_0,
  input  b_0,
  output x_3,
  output x_2,
  output x_1,
  output x_0,
  output A_lt_B,
  output A_gt_B,
  output A_eq_B
);

  wire and_1_out, and_2_out, and_3_out, and_4_out, and_5_out, and_6_out, and_7_out, and_8_out, and_9_out,
       and_10_out, and_11_out, and_12_out, and_13_out, and_14_out, not_1_out, not_2_out, not_3_out,
       not_4_out, not_5_out, not_6_out, not_7_out, not_8_out;

  not not_1 (not_1_out, a_3);
  not not_2 (not_2_out, b_3);
  not not_3 (not_3_out, a_2);
  not not_4 (not_4_out, b_2);
  not not_5 (not_5_out, a_1);
  not not_6 (not_6_out, b_1);
  not not_7 (not_7_out, a_0);
  not not_8 (not_8_out, b_0);
  and and_1 (and_1_out, not_1_out, b_3);
  and and_2 (and_2_out, a_3, not_2_out);
  and and_3 (and_3_out, not_3_out, b_2);
  and and_4 (and_4_out, a_2, not_4_out);
  and and_5 (and_5_out, not_5_out, b_1);
  and and_6 (and_6_out, a_1, not_6_out);
  and and_7 (and_7_out, not_7_out, b_0);
  and and_8 (and_8_out, a_0, not_8_out);
  nor nor_1 (x_3, and_1_out, and_2_out);
  nor nor_2 (x_2, and_3_out, and_4_out);
  nor nor_3 (x_1, and_5_out, and_6_out);
  nor nor_4 (x_0, and_7_out, and_8_out);
  and and_9 (and_9_out, x_3, and_3_out);
  and and_10 (and_10_out, x_3, and_4_out);
  and and_11 (and_11_out, x_3, x_2, and_5_out);
  and and_12 (and_12_out, x_3, x_2, and_6_out);
  and and_13 (and_13_out, x_3, x_2, x_1, and_7_out);
  and and_14 (and_14_out, x_3, x_2, x_1, and_8_out);
  and and_15 (A_eq_B, x_3, x_2, x_1, x_0);
  or or_1 (A_lt_B, and_1_out, and_9_out, and_11_out, and_13_out);
  or or_2 (A_gt_B, and_2_out, and_10_out, and_12_out, and_14_out);
endmodule
