// Digital circuit compt8.dig as structural Verilog
module compt8 (
  input  C,
  output Z_2,
  output Z_1,
  output Z_0
);

  wire and_1_out, and_2_out, and_3_out, and_4_out, and_5_out, not_1_out, not_2_out, not_3_out, or_1_out,
       or_2_out;

  not not_1 (not_1_out, Z_2);
  not not_2 (not_2_out, Z_1);
  not not_3 (not_3_out, Z_0);
  and and_1 (and_1_out, Z_0, Z_1, not_1_out);
  and and_2 (and_2_out, not_3_out, Z_2);
  and and_3 (and_3_out, not_2_out, Z_2);
  and and_4 (and_4_out, Z_0, not_2_out);
  and and_5 (and_5_out, not_3_out, Z_1);
  or or_1 (or_1_out, and_1_out, and_2_out, and_3_out);
  or or_2 (or_2_out, and_4_out, and_5_out);
  D_FF Z_2_n (.D(or_1_out), .C(C), .Q(Z_2));  // open: nQ
  D_FF Z_1_n (.D(or_2_out), .C(C), .Q(Z_1));  // open: nQ
  D_FF Z_0_n (.D(not_3_out), .C(C), .Q(Z_0));  // open: nQ

  // Notes on the sheet:
  //   C: Hz: 2
endmodule
