// Digital circuit compt_4bits.dig as structural Verilog
module compt_4bits (
  input  E,
  input  clk,
  output A_0,
  output A_1,
  output A_2,
  output A_3,
  output Prochain
);

  wire and_1_out, and_2_out, and_3_out;

  and and_1 (and_1_out, A_0, E);
  and and_2 (and_2_out, A_1, and_1_out);
  and and_3 (and_3_out, A_2, and_2_out);
  and and_4 (Prochain, A_3, and_3_out);
  JK_FF jk_ff_1 (.J(E), .C(clk), .K(E), .Q(A_0));  // open: nQ
  JK_FF jk_ff_2 (.J(and_1_out), .C(clk), .K(and_1_out), .Q(A_1));  // open: nQ
  JK_FF jk_ff_3 (.J(and_2_out), .C(clk), .K(and_2_out), .Q(A_2));  // open: nQ
  JK_FF jk_ff_4 (.J(and_3_out), .C(clk), .K(and_3_out), .Q(A_3));  // open: nQ
endmodule
