// Digital circuit compt_mod13.dig as structural Verilog
module compt_mod13 (
  input  clk,
  output A_0,
  output A_1,
  output A_2,
  output A_3
);

  wire and_1_out, not_1_out;

  not not_1 (not_1_out, and_1_out);
  comptchargement comptchargement_1 (
    .Cpt(not_1_out), .Ch(and_1_out), .C(clk), .I_0(1'b0), .I_1(1'b0), .I_2(1'b0), .I_3(1'b0), .A_0(A_0),
    .A_1(A_1), .A_2(A_2), .A_3(A_3));  // open: ov
  and and_1 (and_1_out, A_2, A_3);
endmodule
