// Digital circuit compt_updown.dig as structural Verilog
module compt_updown (
  input  Up,
  input  Down,
  input  clk,
  output A_0,
  output A_1,
  output A_2,
  output A_3
);

  wire and_1_out, and_2_out, and_3_out, and_4_out, and_5_out, and_6_out, and_7_out, jk_ff_1_nq, jk_ff_2_nq,
       jk_ff_3_nq, not_1_out, or_1_out, or_2_out, or_3_out, or_4_out;

  not not_1 (not_1_out, Up);
  and and_1 (and_1_out, not_1_out, Down);
  and and_2 (and_2_out, jk_ff_1_nq, and_1_out);
  and and_3 (and_3_out, jk_ff_2_nq, and_2_out);
  and and_4 (and_4_out, jk_ff_3_nq, and_3_out);
  or or_1 (or_1_out, Up, and_1_out);
  and and_5 (and_5_out, A_0, Up);
  or or_2 (or_2_out, and_5_out, and_2_out);
  and and_6 (and_6_out, A_1, and_5_out);
  or or_3 (or_3_out, and_6_out, and_3_out);
  and and_7 (and_7_out, A_2, and_6_out);
  or or_4 (or_4_out, and_7_out, and_4_out);
  JK_FF jk_ff_1 (.J(or_1_out), .C(clk), .K(or_1_out), .Q(A_0), .nQ(jk_ff_1_nq));
  JK_FF jk_ff_2 (.J(or_2_out), .C(clk), .K(or_2_out), .Q(A_1), .nQ(jk_ff_2_nq));
  JK_FF jk_ff_3 (.J(or_3_out), .C(clk), .K(or_3_out), .Q(A_2), .nQ(jk_ff_3_nq));
  JK_FF jk_ff_4 (.J(or_4_out), .C(clk), .K(or_4_out), .Q(A_3));  // open: nQ
endmodule
