// Digital circuit comptchargement.dig as structural Verilog
module comptchargement (
  input  Cpt,
  input  Ch,
  input  C,
  input  I_0,
  input  I_1,
  input  I_2,
  input  I_3,
  output ov,
  output A_0,
  output A_1,
  output A_2,
  output A_3
);

  wire and_1_out, and_2_out, and_3_out, and_4_out, and_5_out, and_6_out, and_7_out, and_8_out, and_9_out,
       and_10_out, and_11_out, and_12_out, not_1_out, not_2_out, not_3_out, not_4_out, not_5_out, not_6_out,
       or_1_out, or_2_out, or_3_out, or_4_out, or_5_out, or_6_out, or_7_out, or_8_out;

  not not_1 (not_1_out, Ch);
  not not_2 (not_2_out, not_1_out);
  not not_3 (not_3_out, I_0);
  not not_4 (not_4_out, I_1);
  not not_5 (not_5_out, I_2);
  not not_6 (not_6_out, I_3);
  and and_1 (and_1_out, Cpt, not_1_out);
  and and_2 (and_2_out, not_2_out, I_0);
  and and_3 (and_3_out, not_2_out, not_3_out);
  and and_4 (and_4_out, not_2_out, I_1);
  and and_5 (and_5_out, not_2_out, not_4_out);
  and and_6 (and_6_out, not_2_out, I_2);
  and and_7 (and_7_out, not_2_out, not_5_out);
  and and_8 (and_8_out, not_2_out, I_3);
  and and_9 (and_9_out, not_2_out, not_6_out);
  and and_10 (and_10_out, and_1_out, A_0);
  and and_11 (and_11_out, and_1_out, A_0, A_1);
  and and_12 (and_12_out, and_1_out, A_0, A_1, A_2);
  and and_13 (ov, A_3, A_2, A_1, A_0, and_1_out);
  or or_1 (or_1_out, and_2_out, and_1_out);
  or or_2 (or_2_out, and_3_out, and_1_out);
  or or_3 (or_3_out, and_4_out, and_10_out);
  or or_4 (or_4_out, and_10_out, and_5_out);
  or or_5 (or_5_out, and_6_out, and_11_out);
  or or_6 (or_6_out, and_11_out, and_7_out);
  or or_7 (or_7_out, and_8_out, and_12_out);
  or or_8 (or_8_out, and_12_out, and_9_out);
  JK_FF Z_0_n (.J(or_1_out), .C(C), .K(or_2_out), .Q(A_0));  // open: nQ
  JK_FF Z_1_n (.J(or_3_out), .C(C), .K(or_4_out), .Q(A_1));  // open: nQ
  JK_FF Z_2_n (.J(or_5_out), .C(C), .K(or_6_out), .Q(A_2));  // open: nQ
  JK_FF Z_3_n (.J(or_7_out), .C(C), .K(or_8_out), .Q(A_3));  // open: nQ

  // Notes on the sheet:
  //   C: Hz: 2
endmodule
