// Digital circuit course.dig as structural Verilog
module course (
  input  a,
  output s
);

  wire not_1_out;

  not not_1 (not_1_out, a);
  and and_1 (s, a, not_1_out);

  // Notes on the sheet:
  //   a'
endmodule
