// Digital circuit debounce.dig as structural Verilog
module debounce (
  output Q,
  output Qb
);

  wire nand_2_out, pullup_1_out, switchdt_2_p2, switchdt_2_p3;

  PullUp pullup_1 (.out(pullup_1_out));
  // SwitchDT switchdt_1: pin names not known; wires that end beside it: pullup_1_out, 1'b0, Qb
  // SwitchDT switchdt_2: pin names not known; wires that end beside it: 1'b0, switchdt_2_p2, switchdt_2_p3
  PullUp pullup_2 (.out(switchdt_2_p2));
  PullUp pullup_3 (.out(switchdt_2_p3));
  nand nand_1 (Q, switchdt_2_p2, nand_2_out);
  nand nand_2 (nand_2_out, Q, switchdt_2_p3);
endmodule
