// Digital circuit decod3_8.dig as structural Verilog
module decod3_8 (
  input  z,
  input  y,
  input  x,
  output D_0_eq_x_y_z,
  output D_1_eq_x_y_z,
  output D_2_eq_x_yz,
  output D_3_eq_x_yz,
  output D_4_eq_xy_z,
  output D_5_eq_xy_z,
  output D_6_eq_xyz,
  output D_7_eq_xyz
);

  wire not_1_out, not_2_out, not_3_out;

  not not_1 (not_1_out, x);
  not not_2 (not_2_out, y);
  not not_3 (not_3_out, z);
  and and_1 (D_0_eq_x_y_z, not_1_out, not_2_out, not_3_out);
  and and_2 (D_1_eq_x_y_z, not_1_out, not_2_out, z);
  and and_3 (D_2_eq_x_yz, not_1_out, y, not_3_out);
  and and_4 (D_3_eq_x_yz, not_1_out, y, z);
  and and_5 (D_4_eq_xy_z, x, not_2_out, not_3_out);
  and and_6 (D_5_eq_xy_z, x, not_2_out, z);
  and and_7 (D_6_eq_xyz, x, y, not_3_out);
  and and_8 (D_7_eq_xyz, z, y, x);
endmodule
