// Digital circuit decode2_4_enable.dig as structural Verilog
module decode2_4_enable (
  input  E,
  input  y,
  input  x,
  output D_0,
  output D_1,
  output D_2,
  output D_3
);

  wire not_1_out, not_2_out, not_3_out;

  not not_1 (not_1_out, x);
  not not_2 (not_2_out, y);
  not not_3 (not_3_out, E);
  nand nand_1 (D_0, not_1_out, not_2_out, not_3_out);
  nand nand_2 (D_1, not_1_out, y, not_3_out);
  nand nand_3 (D_2, x, not_2_out, not_3_out);
  nand nand_4 (D_3, x, y, not_3_out);
endmodule
