// Digital circuit demi_add.dig as structural Verilog
module demi_add (
  input  a_i,
  input  b_i,
  output S_i,
  output R_i
);

  wire and_1_out, and_2_out, not_1_out, not_2_out;

  not not_1 (not_1_out, a_i);
  not not_2 (not_2_out, b_i);
  and and_1 (and_1_out, a_i, not_2_out);
  and and_2 (and_2_out, not_1_out, b_i);
  and and_3 (R_i, b_i, a_i);
  or or_1 (S_i, and_1_out, and_2_out);
endmodule
