// Digital circuit demi_add_xor.dig as structural Verilog
module demi_add_xor (
  input  a_i,
  input  b_i,
  output S_i,
  output R_i
);

  xor xor_1 (S_i, a_i, b_i);
  and and_1 (R_i, b_i, a_i);
endmodule
