// Digital circuit demux8.dig as structural Verilog
module demux8 (
  input  s_0,
  input  s_1,
  input  s_2,
  input  I,
  output O_0,
  output O_1,
  output O_2,
  output O_3,
  output O_4,
  output O_5,
  output O_6,
  output O_7
);

  wire not_1_out, not_2_out, not_3_out;

  not not_1 (not_1_out, s_2);
  not not_2 (not_2_out, s_1);
  not not_3 (not_3_out, s_0);
  and and_1 (O_0, not_1_out, not_2_out, not_3_out, I);
  and and_2 (O_1, not_1_out, not_2_out, s_0, I);
  and and_3 (O_2, not_1_out, s_1, not_3_out, I);
  and and_4 (O_3, not_1_out, s_1, s_0, I);
  and and_5 (O_4, s_2, not_2_out, not_3_out, I);
  and and_6 (O_5, s_2, not_2_out, s_0, I);
  and and_7 (O_6, s_2, s_1, not_3_out, I);
  and and_8 (O_7, s_0, s_1, s_2, I);
endmodule
