// Digital circuit encode1.dig as structural Verilog
module encode1 (
  input  D_1,
  input  D_2,
  input  D_3,
  input  D_4,
  input  D_5,
  input  D_6,
  input  D_7,
  output x,
  output y,
  output z
);

  or or_1 (x, D_4, D_5, D_6, D_7);
  or or_2 (y, D_2, D_3, D_6, D_7);
  or or_3 (z, D_1, D_3, D_5, D_7);
endmodule
