// Digital circuit encode_pri.dig as structural Verilog
module encode_pri (
  input  D_0,
  input  D_1,
  input  D_2,
  input  D_3,
  output x,
  output y,
  output V
);

  wire and_1_out, not_1_out;

  not not_1 (not_1_out, D_2);
  or or_1 (x, D_2, D_3);
  and and_1 (and_1_out, D_1, not_1_out);
  or or_2 (V, D_0, D_1, D_2, D_3);
  or or_3 (y, and_1_out, D_3);
endmodule
