// Digital circuit exbloc2a.dig as structural Verilog
module exbloc2a (
  input  a,
  input  b,
  input  c,
  input  d,
  output S
);

  wire nand_1_out, nand_2_out, nand_3_out, nand_4_out, undriven, undriven_2, undriven_3, undriven_4;

  nand nand_1 (nand_1_out, undriven, undriven_2);
  nand nand_2 (nand_2_out, undriven_3, undriven_4);
  // NAnd nand_3 has open pins: In_1=open, In_2=open, out=nand_3_out
  // NAnd nand_4 has open pins: In_1=open, In_2=open, out=nand_4_out

  // Notes on the sheet:
  //   -
endmodule
