// Digital circuit exbloc2b.dig as structural Verilog
module exbloc2b (
  input  a_3,
  input  a_2,
  input  a_1,
  input  a_0,
  output S
);

  wire nand_1_out, nand_2_out, nand_3_out, not_1_out, not_2_out, not_3_out, not_4_out, undriven, undriven_2,
       undriven_3, undriven_4, undriven_5, undriven_6, undriven_7, undriven_8, undriven_9, undriven_10,
       undriven_11, undriven_12;

  not not_1 (not_1_out, undriven);
  not not_2 (not_2_out, undriven_2);
  not not_3 (not_3_out, undriven_3);
  not not_4 (not_4_out, undriven_4);
  nand nand_1 (nand_1_out, undriven_5, undriven_6);
  nand nand_2 (nand_2_out, undriven_7, undriven_8);
  nand nand_3 (nand_3_out, undriven_9, undriven_10, undriven_11, undriven_12);
endmodule
