// Digital circuit exbloc3a.dig as structural Verilog
module exbloc3a (
  input  z_0,
  input  z_1,
  input  y_0,
  input  y_1,
  input  y_2,
  output P_0,
  output P_1,
  output P_2,
  output P_3,
  output P_4
);

  wire add_2_c_o, add_3_c_o, add_4_c_o, and_1_out, and_2_out, and_3_out, and_4_out, and_5_out, and_6_out,
       undriven, undriven_2, undriven_3, undriven_4, undriven_5, undriven_6, undriven_7, undriven_8,
       undriven_9, undriven_10, undriven_11, undriven_12, undriven_13, undriven_14, undriven_15, undriven_16,
       undriven_17, undriven_18, undriven_19, undriven_20;

  and and_1 (and_1_out, undriven, undriven_2);
  and and_2 (and_2_out, undriven_3, undriven_4);
  and and_3 (and_3_out, undriven_5, undriven_6);
  and and_4 (and_4_out, undriven_7, undriven_8);
  and and_5 (and_5_out, undriven_9, undriven_10);
  and and_6 (and_6_out, undriven_11, undriven_12);
  Add add_1 (.a(undriven_13), .b(undriven_14), .c_i(add_2_c_o), .s(P_3), .c_o(P_4));
  Add add_2 (.a(undriven_15), .b(undriven_16), .c_i(add_3_c_o), .s(P_2), .c_o(add_2_c_o));
  Add add_3 (.a(undriven_17), .b(undriven_18), .c_i(add_4_c_o), .s(P_1), .c_o(add_3_c_o));
  Add add_4 (.a(undriven_19), .b(undriven_20), .c_i(1'b0), .s(P_0), .c_o(add_4_c_o));
endmodule
