// Digital circuit exbloc3c.dig as structural Verilog
module exbloc3c (
  input  a,
  input  b,
  input  c,
  input  d,
  output F
);

  wire decoder_1_out_0, decoder_1_out_1, decoder_1_out_2, decoder_1_out_3;

  Decoder #(.Selector_Bits(2)) decoder_1 (
    .sel({b, a}), .out_0(decoder_1_out_0), .out_1(decoder_1_out_1), .out_2(decoder_1_out_2),
    .out_3(decoder_1_out_3));
  Multiplexer #(.Selector_Bits(2)) multiplexer_1 (
    .sel({d, c}), .in_0(decoder_1_out_0), .in_1(decoder_1_out_1), .in_2(decoder_1_out_2),
    .in_3(decoder_1_out_3), .out(F));
endmodule
