// Digital circuit exbloc3d.dig as structural Verilog
module exbloc3d (
  input  A,
  input  B,
  input  C,
  input  D
);

  wire not_1_out;

  not not_1 (not_1_out, A);
  Multiplexer #(.Selector_Bits(3)) multiplexer_1 (
    .sel({D, C, B}), .in_0(1'b1), .in_1(A), .in_2(not_1_out), .in_3(1'b0), .in_4(1'b0), .in_5(not_1_out),
    .in_6(A), .in_7(1'b1));  // open: out
endmodule
