// Digital circuit exbloc3e.dig as structural Verilog
module exbloc3e (
  input  A,
  input  B,
  input  C,
  output F,
  output T,
  output U,
  output Y,
  output X,
  output Z_3,
  output Z_2,
  output Z_1
);

  not not_1 (T, B);
  not not_2 (U, C);
  and and_1 (X, T, A);
  or or_1 (Y, A, T);
  not not_3 (Z_1, Y);
  and and_2 (Z_2, X, U);
  and and_3 (Z_3, X, C);
  or or_2 (F, Z_1, Z_2, Z_3);
endmodule
