// Digital circuit exbloc4a.dig as structural Verilog
module exbloc4a (
  input  x,
  input  y,
  input  clk,
  output A,
  output B,
  output S,
  output Z
);

  wire nor_1_out, nor_2_out, nor_3_out;

  D_FF d_ff_1 (.D(x), .C(clk), .Q(A));  // open: nQ
  JK_FF jk_ff_1 (.J(1'b1), .C(clk), .K(y), .Q(B));  // open: nQ
  nor nor_1 (nor_1_out, A, B);
  nor nor_2 (nor_2_out, A, nor_1_out);
  nor nor_3 (nor_3_out, nor_1_out, B);
  or or_1 (S, nor_2_out, nor_3_out);
  D_FF d_ff_2 (.D(S), .C(clk), .nQ(Z));  // open: Q
endmodule
