// Digital circuit exbloc4b.dig as structural Verilog
module exbloc4b (
  input  A,
  input  B,
  output S,
  output S_2
);

  wire and_1_out, and_2_out;

  and and_1 (and_1_out, A, B);
  and and_2 (and_2_out, ~B, S);  // And
  nor nor_1 (S_2, and_1_out, and_2_out);
  not not_1 (S, S_2);
endmodule
