// Digital circuit exbloc4c.dig as structural Verilog
module exbloc4c (
  input  B,
  input  clk,
  input  A,
  output S,
  output Y,
  output X,
  output X_2
);

  D_FF d_ff_1 (.D(B), .C(clk), .Q(X), .nQ(X_2));
  JK_FF jk_ff_1 (.J(A), .C(X), .K(1'b1), .Q(Y));  // open: nQ
  xnor xnor_1 (S, Y, X_2);
endmodule
