// Digital circuit exbloc4d.dig as structural Verilog
module exbloc4d (
  input  clk,
  input  B,
  input  A,
  output S
);

  wire xor_1_out;

  JK_FF jk_ff_1 (.J(xor_1_out), .C(clk), .K(B), .Q(S));  // open: nQ
  xor xor_1 (xor_1_out, S, A);
endmodule
