// Digital circuit exbloc4e.dig as structural Verilog
module exbloc4e (
  input  clk,
  input  in_3,
  output out_1
);

  wire and_1_out, d_ff_1_q, d_ff_2_q, d_ff_3_nq, nor_1_out, nor_2_out, nor_3_out;

  D_FF d_ff_1 (.D(in_3), .C(clk), .Q(d_ff_1_q));  // open: nQ
  nor nor_1 (nor_1_out, d_ff_2_q, d_ff_1_q);
  and and_1 (and_1_out, d_ff_1_q, d_ff_3_nq);
  nor nor_2 (nor_2_out, nor_1_out, and_1_out);
  D_FF d_ff_2 (.D(nor_2_out), .C(clk), .Q(d_ff_2_q));  // open: nQ
  nor nor_3 (nor_3_out, d_ff_2_q, d_ff_3_nq);
  D_FF d_ff_3 (.D(nor_3_out), .C(clk), .Q(out_1), .nQ(d_ff_3_nq));
endmodule
