// Digital circuit exemp_seq101.dig as structural Verilog
module exemp_seq101 (
  input  A,
  input  C,
  output S
);

  wire and_1_out, and_2_out, and_3_out, not_1_out, or_1_out, or_2_out, Z_0_n_q, Z_1_n_q;

  not not_1 (not_1_out, A);
  and and_1 (and_1_out, not_1_out, Z_0_n_q);
  and and_2 (and_2_out, A, Z_1_n_q);
  and and_3 (and_3_out, Z_0_n_q, Z_1_n_q);
  and and_4 (S, Z_0_n_q, Z_1_n_q);
  or or_1 (or_1_out, and_1_out, and_2_out);
  or or_2 (or_2_out, A, and_3_out);
  D_FF Z_1_n (.D(or_1_out), .C(C), .Q(Z_1_n_q));  // open: nQ
  D_FF Z_0_n (.D(or_2_out), .C(C), .Q(Z_0_n_q));  // open: nQ

  // Notes on the sheet:
  //   C: Hz: 2
endmodule
