// Digital circuit exemp_seq101JK.dig as structural Verilog
module exemp_seq101JK (
  input  A,
  input  C,
  output S
);

  wire and_1_out, and_2_out, nor_1_out, not_1_out, not_2_out, Z_0_n, Z_1_n;

  not not_1 (not_1_out, A);
  not not_2 (not_2_out, Z_0_n);
  and and_1 (and_1_out, not_1_out, Z_0_n);
  and and_2 (and_2_out, not_1_out, not_2_out);
  nor nor_1 (nor_1_out, A, Z_1_n);
  and and_3 (S, Z_0_n, Z_1_n);
  JK_FF u_Z_1_n (.J(and_1_out), .C(C), .K(and_2_out), .Q(Z_1_n));  // open: nQ
  JK_FF u_Z_0_n (.J(A), .C(C), .K(nor_1_out), .Q(Z_0_n));  // open: nQ
  // Probe seq_101.fsm on {Z_1_n, Z_0_n}

  // Notes on the sheet:
  //   C: Hz: 2
endmodule
