// Digital circuit exemple_seq1.dig as structural Verilog
module exemple_seq1 (
  input  I,
  input  C,
  output S,
  output U
);

  wire and_1_out, and_2_out, and_3_out, not_1_out, or_1_out, or_2_out, Z_0_n, Z_1_n;

  not not_1 (not_1_out, Z_1_n);
  and and_1 (and_1_out, I, Z_1_n);
  and and_2 (and_2_out, I, not_1_out);
  and and_3 (and_3_out, I, Z_0_n);
  and and_4 (S, Z_0_n, not_1_out);
  and and_5 (U, Z_0_n, Z_1_n);
  or or_1 (or_1_out, and_1_out, Z_0_n);
  or or_2 (or_2_out, and_2_out, and_3_out);
  D_FF u_Z_1_n (.D(or_1_out), .C(C), .Q(Z_1_n));  // open: nQ
  D_FF u_Z_0_n (.D(or_2_out), .C(C), .Q(Z_0_n));  // open: nQ
  // Probe state on {Z_1_n, Z_0_n}

  // Notes on the sheet:
  //   C: Hz: 2
endmodule
