// Digital circuit exemple_seq1_run.dig as structural Verilog
module exemple_seq1_run (
  input  I,
  input  C,
  output S,
  output U
);

  wire and_1_out, and_2_out, and_3_out, not_1_out, or_1_out, or_2_out;
  wire [1:0] Z_0_n_q;

  not not_1 (not_1_out, Z_0_n_q[1]);
  and and_1 (and_1_out, I, Z_0_n_q[1]);
  and and_2 (and_2_out, I, not_1_out);
  and and_3 (and_3_out, I, Z_0_n_q[0]);
  and and_4 (S, Z_0_n_q[0], not_1_out);
  and and_5 (U, Z_0_n_q[0], Z_0_n_q[1]);
  or or_1 (or_1_out, and_1_out, Z_0_n_q[0]);
  or or_2 (or_2_out, and_2_out, and_3_out);
  D_FF Z_1_n (.D(or_1_out), .C(C), .Q(Z_0_n_q[1]));  // open: nQ
  D_FF Z_0_n (.D(or_2_out), .C(C), .Q(Z_0_n_q[0]));  // open: nQ
  // Probe état on Z_0_n_q

  // Notes on the sheet:
  //   C: Hz: 2
endmodule
