// Digital circuit fonct_arbit_decod.dig as structural Verilog
module fonct_arbit_decod (
  input  [2:0] I,
  output Y
);

  wire decoder_1_out_0, decoder_1_out_2, decoder_1_out_5, decoder_1_out_6;

  Decoder #(.Selector_Bits(3)) decoder_1 (
    .sel(I), .out_0(decoder_1_out_0), .out_2(decoder_1_out_2), .out_5(decoder_1_out_5),
    .out_6(decoder_1_out_6));  // open: out_1, out_3, out_4, out_7
  or or_1 (Y, decoder_1_out_0, decoder_1_out_2, decoder_1_out_5, decoder_1_out_6);
endmodule
