// Digital circuit fulladderR.dig as structural Verilog
module fulladderR (
  input  a_i,
  input  b_i,
  input  r_i_1,
  output R_i
);

  wire and_1_out, and_2_out, and_3_out;

  and and_1 (and_1_out, a_i, b_i);
  and and_2 (and_2_out, a_i, r_i_1);
  and and_3 (and_3_out, b_i, r_i_1);
  or or_1 (R_i, and_1_out, and_2_out, and_3_out);
endmodule
