// Digital circuit fulladderS.dig as structural Verilog
module fulladderS (
  input  a_i,
  input  b_i,
  input  r_i_1,
  output S_i
);

  wire and_1_out, and_2_out, and_3_out, and_4_out, not_1_out, not_2_out, not_3_out;

  not not_1 (not_1_out, a_i);
  not not_2 (not_2_out, b_i);
  not not_3 (not_3_out, r_i_1);
  and and_1 (and_1_out, not_1_out, not_2_out, r_i_1);
  and and_2 (and_2_out, not_1_out, b_i, not_3_out);
  and and_3 (and_3_out, a_i, not_2_out, not_3_out);
  and and_4 (and_4_out, not_1_out, b_i, r_i_1);
  or or_1 (S_i, and_1_out, and_2_out, and_3_out, and_4_out);
endmodule
