// Digital circuit fulladder_xorPG.dig as structural Verilog
module fulladder_xorPG (
  input  a_i,
  input  b_i,
  input  r_i_1,
  output S_i,
  output R_i,
  output P_i,
  output G_i
);

  wire and_2_out;

  xor xor_1 (P_i, a_i, b_i);
  and and_1 (G_i, b_i, a_i);
  xor xor_2 (S_i, P_i, r_i_1);
  and and_2 (and_2_out, P_i, r_i_1);
  or or_1 (R_i, and_2_out, G_i);
endmodule
