// Digital circuit fulladderxor.dig as structural Verilog
module fulladderxor (
  input  a_i,
  input  b_i,
  input  r_i_1,
  output S_i,
  output R_i
);

  wire and_1_out, and_2_out, xor_1_out;

  xor xor_1 (xor_1_out, a_i, b_i);
  and and_1 (and_1_out, b_i, a_i);
  xor xor_2 (S_i, xor_1_out, r_i_1);
  and and_2 (and_2_out, xor_1_out, r_i_1);
  or or_1 (R_i, and_2_out, and_1_out);
endmodule
