// Digital circuit johnson2_quad.dig as structural Verilog
module johnson2_quad (
  input  clk,
  output H,
  output Q_a,
  output Q__a,
  output Q_b,
  output Q__b
);

  D_FF d_ff_1 (.D(Q__b), .C(clk), .Q(Q_a), .nQ(Q__a));
  D_FF d_ff_2 (.D(Q_a), .C(clk), .Q(Q_b), .nQ(Q__b));

  assign H = clk;
endmodule
