// Digital circuit johnson2_quad_decode.dig as structural Verilog
module johnson2_quad_decode (
  input  clk,
  output a,
  output b,
  output c,
  output d,
  output H
);

  wire d_ff_1_nq, d_ff_1_q, d_ff_2_nq, d_ff_2_q;

  D_FF d_ff_1 (.D(d_ff_2_nq), .C(clk), .Q(d_ff_1_q), .nQ(d_ff_1_nq));
  D_FF d_ff_2 (.D(d_ff_1_q), .C(clk), .Q(d_ff_2_q), .nQ(d_ff_2_nq));
  and and_1 (a, d_ff_2_nq, d_ff_1_q);
  and and_2 (c, d_ff_1_nq, d_ff_2_q);
  and and_3 (b, d_ff_2_q, d_ff_1_q);
  and and_4 (d, d_ff_2_nq, d_ff_1_nq);

  assign H = clk;
endmodule
