// Digital circuit johnson4.dig as structural Verilog
module johnson4 (
  input  clk,
  output a,
  output b,
  output c,
  output d
);

  wire d_ff_4_nq;

  D_FF d_ff_1 (.D(d_ff_4_nq), .C(clk), .Q(a));  // open: nQ
  D_FF d_ff_2 (.D(a), .C(clk), .Q(b));  // open: nQ
  D_FF d_ff_3 (.D(b), .C(clk), .Q(c));  // open: nQ
  D_FF d_ff_4 (.D(c), .C(clk), .Q(d), .nQ(d_ff_4_nq));
endmodule
