// Digital circuit lookahead1.dig as structural Verilog
module lookahead1 (
  input  G_0,
  input  P_0,
  input  R_0,
  input  G_1,
  input  G_2,
  input  P_1,
  input  P_2,
  output R_3,
  output R_2,
  output R_1
);

  wire and_1_out, and_2_out, and_3_out, and_4_out, and_5_out, and_6_out;

  and and_1 (and_1_out, R_0, P_0, P_1, P_2);
  and and_2 (and_2_out, G_0, P_1, P_2);
  and and_3 (and_3_out, G_1, P_2);
  and and_4 (and_4_out, R_0, P_0, P_1);
  and and_5 (and_5_out, G_0, P_1);
  and and_6 (and_6_out, R_0, P_0);
  or or_1 (R_3, and_1_out, and_2_out, and_3_out, G_2);
  or or_2 (R_2, and_4_out, and_5_out, G_1);
  or or_3 (R_1, and_6_out, G_0);
endmodule
