// Digital circuit mux2.dig as structural Verilog
module mux2 (
  input  I_0,
  input  I_1,
  input  S,
  output Y
);

  wire and_1_out, and_2_out, not_1_out;

  not not_1 (not_1_out, S);
  and and_1 (and_1_out, I_0, not_1_out);
  and and_2 (and_2_out, I_1, S);
  or or_1 (Y, and_1_out, and_2_out);
endmodule
