// Digital circuit mux2symb.dig as structural Verilog
module mux2symb (
  input  I_0,
  input  I_1,
  input  S,
  output Y
);

  Multiplexer multiplexer_1 (.sel(S), .in_0(I_0), .in_1(I_1), .out(Y));
endmodule
