// Digital circuit mux4.dig as structural Verilog
module mux4 (
  input  S_0,
  input  S_1,
  input  I_0,
  input  I_1,
  input  I_2,
  input  I_3,
  output Y
);

  wire and_1_out, and_2_out, and_3_out, and_4_out, not_1_out, not_2_out;

  not not_1 (not_1_out, S_0);
  not not_2 (not_2_out, S_1);
  and and_1 (and_1_out, I_0, not_1_out, not_2_out);
  and and_2 (and_2_out, I_1, S_0, not_2_out);
  and and_3 (and_3_out, I_2, not_1_out, S_1);
  and and_4 (and_4_out, I_3, S_0, S_1);
  or or_1 (Y, and_1_out, and_2_out, and_3_out, and_4_out);
endmodule
