// Digital circuit mux4symb.dig as structural Verilog
module mux4symb (
  input  I_0,
  input  I_1,
  input  [1:0] S,
  input  I_2,
  input  I_3,
  output Y
);

  Multiplexer #(.Selector_Bits(2)) multiplexer_1 (.sel(S), .in_0(I_0), .in_1(I_1), .in_2(I_2), .in_3(I_3), .out(Y));
endmodule
