// Digital circuit mux_4_1_3s.dig as structural Verilog
module mux_4_1_3s (
  input  I_0,
  input  I_1,
  input  I_2,
  input  I_3,
  input  [1:0] Selec,
  input  E,
  output Y
);

  wire and_1_out, and_2_out, and_3_out, and_4_out, decoder_1_out_0, decoder_1_out_1, decoder_1_out_2,
       decoder_1_out_3;

  Decoder #(.Selector_Bits(2)) decoder_1 (
    .sel(Selec), .out_0(decoder_1_out_0), .out_1(decoder_1_out_1), .out_2(decoder_1_out_2),
    .out_3(decoder_1_out_3));
  and and_1 (and_1_out, E, decoder_1_out_0);
  and and_2 (and_2_out, E, decoder_1_out_1);
  and and_3 (and_3_out, E, decoder_1_out_2);
  and and_4 (and_4_out, E, decoder_1_out_3);
  assign Y = and_1_out ? I_0 : 1'bz;  // Driver driver_1
  assign Y = and_2_out ? I_1 : 1'bz;  // Driver driver_2
  assign Y = and_3_out ? I_2 : 1'bz;  // Driver driver_3
  assign Y = and_4_out ? I_3 : 1'bz;  // Driver driver_4
endmodule
