// Digital circuit pal_proto.dig as structural Verilog
module pal_proto (
  input  b,
  input  c,
  input  d,
  input  a,
  output F_1,
  output F_2,
  output F_3
);

  wire and_1_out, and_2_out, and_3_out, and_4_out, and_5_out, and_6_out, and_7_out, and_8_out, and_9_out,
       not_1_out, not_2_out, not_3_out, not_4_out, not_5_out, undriven, undriven_2, undriven_3, undriven_4,
       undriven_5, undriven_6, undriven_7, undriven_8, undriven_9;

  not not_1 (not_1_out, a);
  not not_2 (not_2_out, b);
  not not_3 (not_3_out, c);
  not not_4 (not_4_out, d);
  buf and_1 (and_1_out, undriven);  // And open: In_2
  buf and_2 (and_2_out, undriven_2);  // And open: In_2
  buf and_3 (and_3_out, undriven_3);  // And open: In_2
  buf and_4 (and_4_out, undriven_4);  // And open: In_2
  buf and_5 (and_5_out, undriven_5);  // And open: In_2
  buf and_6 (and_6_out, undriven_6);  // And open: In_2
  buf and_7 (and_7_out, undriven_7);  // And open: In_2
  buf and_8 (and_8_out, undriven_8);  // And open: In_2
  buf and_9 (and_9_out, undriven_9);  // And open: In_2
  or or_1 (F_1, and_1_out, and_2_out, and_3_out);
  or or_2 (F_2, and_4_out, and_5_out, and_6_out);
  or or_3 (F_3, and_7_out, and_8_out, and_9_out);
  not not_5 (not_5_out, F_1);
endmodule
