// Digital circuit pla_proto.dig as structural Verilog
module pla_proto (
  input  a,
  input  b,
  input  c,
  output F_1,
  output F_0
);

  wire and_1_out, and_2_out, and_3_out, and_4_out, not_1_out, not_2_out, not_3_out, or_1_out, or_2_out,
       undriven, undriven_2, undriven_3, undriven_4, undriven_5, undriven_6, undriven_7, undriven_8;

  not not_1 (not_1_out, a);
  not not_2 (not_2_out, b);
  not not_3 (not_3_out, c);
  buf and_1 (and_1_out, undriven);  // And open: In_2
  buf and_2 (and_2_out, undriven_2);  // And open: In_2
  buf and_3 (and_3_out, undriven_3);  // And open: In_2
  buf and_4 (and_4_out, undriven_4);  // And open: In_2
  buf or_1 (or_1_out, undriven_5);  // Or open: In_2
  buf or_2 (or_2_out, undriven_6);  // Or open: In_2
  xor xor_1 (F_1, undriven_8, or_2_out);
  xor xor_2 (F_0, undriven_7, or_1_out);
endmodule
