// Digital circuit proto_rom.dig as structural Verilog
module proto_rom (
  input  [3:0] Addr,
  output A_3,
  output A_2,
  output A_1,
  output A_0
);

  wire decoder_1_out_0, decoder_1_out_1, decoder_1_out_2, decoder_1_out_3, decoder_1_out_4, decoder_1_out_5,
       decoder_1_out_6, decoder_1_out_7, decoder_1_out_8, decoder_1_out_9, decoder_1_out_10,
       decoder_1_out_11, decoder_1_out_12, decoder_1_out_13, decoder_1_out_14, decoder_1_out_15, undriven,
       undriven_2, undriven_3, undriven_4;

  Decoder #(.Selector_Bits(4)) decoder_1 (
    .sel(Addr), .out_0(decoder_1_out_0), .out_1(decoder_1_out_1), .out_2(decoder_1_out_2),
    .out_3(decoder_1_out_3), .out_4(decoder_1_out_4), .out_5(decoder_1_out_5), .out_6(decoder_1_out_6),
    .out_7(decoder_1_out_7), .out_8(decoder_1_out_8), .out_9(decoder_1_out_9), .out_10(decoder_1_out_10),
    .out_11(decoder_1_out_11), .out_12(decoder_1_out_12), .out_13(decoder_1_out_13),
    .out_14(decoder_1_out_14), .out_15(decoder_1_out_15));
  buf or_1 (A_3, undriven);  // Or open: In_2
  buf or_2 (A_2, undriven_2);  // Or open: In_2
  buf or_3 (A_1, undriven_3);  // Or open: In_2
  buf or_4 (A_0, undriven_4);  // Or open: In_2
endmodule
