// Digital circuit reg_4_paral.dig as structural Verilog
module reg_4_paral (
  input  I_1,
  input  charge,
  input  I_2,
  input  I_3,
  input  I_4,
  input  clk,
  output O_1,
  output O_2,
  output O_3,
  output O_4
);

  wire and_1_out, and_2_out, and_3_out, and_4_out, and_5_out, and_6_out, and_7_out, and_8_out, not_1_out,
       not_2_out, or_1_out, or_2_out, or_3_out, or_4_out;

  not not_1 (not_1_out, charge);
  not not_2 (not_2_out, not_1_out);
  and and_1 (and_1_out, O_1, not_1_out);
  and and_2 (and_2_out, not_2_out, I_1);
  and and_3 (and_3_out, O_2, not_1_out);
  and and_4 (and_4_out, not_2_out, I_2);
  and and_5 (and_5_out, O_3, not_1_out);
  and and_6 (and_6_out, not_2_out, I_3);
  and and_7 (and_7_out, O_4, not_1_out);
  and and_8 (and_8_out, not_2_out, I_4);
  or or_1 (or_1_out, and_1_out, and_2_out);
  or or_2 (or_2_out, and_3_out, and_4_out);
  or or_3 (or_3_out, and_5_out, and_6_out);
  or or_4 (or_4_out, and_7_out, and_8_out);
  D_FF d_ff_1 (.D(or_1_out), .C(clk), .Q(O_1));  // open: nQ
  D_FF d_ff_2 (.D(or_2_out), .C(clk), .Q(O_2));  // open: nQ
  D_FF d_ff_3 (.D(or_3_out), .C(clk), .Q(O_3));  // open: nQ
  D_FF d_ff_4 (.D(or_4_out), .C(clk), .Q(O_4));  // open: nQ
endmodule
