// Digital circuit regist_4.dig as structural Verilog
module regist_4 (
  input  I_1,
  input  I_2,
  input  I_4,
  input  I_3,
  input  [3:0] I,
  input  E,
  input  clk,
  input  clk_2,
  output O_1,
  output O_3,
  output O_4,
  output O_2,
  output [3:0] O
);

  D_FF d_ff_1 (.D(I_1), .C(clk), .Q(O_1));  // open: nQ
  D_FF d_ff_2 (.D(I_2), .C(clk), .Q(O_2));  // open: nQ
  D_FF d_ff_3 (.D(I_3), .C(clk), .Q(O_3));  // open: nQ
  D_FF d_ff_4 (.D(I_4), .C(clk), .Q(O_4));  // open: nQ
  Register #(.Bits(4)) register_1 (.D(I), .C(clk_2), .en(E), .Q(O));
endmodule
