// Digital circuit ring4.dig as structural Verilog
module ring4 (
  input  clk,
  input  Init,
  output a,
  output b,
  output c,
  output d
);

  wire or_1_out;

  or or_1 (or_1_out, d, Init);
  D_FF d_ff_1 (.D(or_1_out), .C(clk), .Q(a));  // open: nQ
  D_FF d_ff_2 (.D(a), .C(clk), .Q(b));  // open: nQ
  D_FF d_ff_3 (.D(b), .C(clk), .Q(c));  // open: nQ
  D_FF d_ff_4 (.D(c), .C(clk), .Q(d));  // open: nQ
endmodule
