// Digital circuit rippleT3.dig as structural Verilog
module rippleT3 (
  input  clk,
  output A_0,
  output A_1,
  output A_2
);

  wire t_ff_1_nq, t_ff_2_nq;

  T_FF t_ff_1 (.T(1'b1), .C(clk), .Q(A_0), .nQ(t_ff_1_nq));
  T_FF t_ff_2 (.T(1'b1), .C(t_ff_1_nq), .Q(A_1), .nQ(t_ff_2_nq));
  T_FF t_ff_3 (.T(1'b1), .C(t_ff_2_nq), .Q(A_2));  // open: nQ
endmodule
