// Digital circuit schema_bascules.dig as structural Verilog
module schema_bascules (
);

  wire Front_descendant_nq, Front_descendant_q, Front_montant_nq, Front_montant_q, undriven, undriven_2,
       undriven_3, undriven_4;

  D_FF Front_montant (.D(undriven), .C(undriven_2), .Q(Front_montant_q), .nQ(Front_montant_nq));
  D_FF Front_descendant (.D(undriven_3), .C(~undriven_4), .Q(Front_descendant_q), .nQ(Front_descendant_nq));
endmodule
