// Digital circuit seq_JKb.dig as structural Verilog
module seq_JKb (
  input  C,
  output Q_0,
  output Q_1
);

  wire and_1_out, nor_1_out, q_1_n_nq;

  and and_1 (and_1_out, q_1_n_nq, Q_0);
  JK_FF q_0_n (.J(q_1_n_nq), .C(C), .K(and_1_out), .Q(Q_0));  // open: nQ
  nor nor_1 (nor_1_out, q_1_n_nq, Q_0);
  JK_FF #(.Default(1)) q_1_n (.J(Q_0), .C(C), .K(nor_1_out), .Q(Q_1), .nQ(q_1_n_nq));
endmodule
