// Digital circuit shift4.dig as structural Verilog
module shift4 (
  input  I,
  input  clk,
  output O
);

  wire d_ff_1_q, d_ff_2_q, d_ff_3_q;

  D_FF d_ff_1 (.D(I), .C(clk), .Q(d_ff_1_q));  // open: nQ
  D_FF d_ff_2 (.D(d_ff_1_q), .C(clk), .Q(d_ff_2_q));  // open: nQ
  D_FF d_ff_3 (.D(d_ff_2_q), .C(clk), .Q(d_ff_3_q));  // open: nQ
  D_FF d_ff_4 (.D(d_ff_3_q), .C(clk), .Q(O));  // open: nQ
endmodule
