// Digital circuit shift4_univ.dig as structural Verilog
module shift4_univ (
  input  I_1,
  input  clk,
  input  I_2,
  input  I_3,
  input  I_4,
  input  G,
  input  D,
  input  [1:0] \Sél ,
  output O_1,
  output O_2,
  output O_3,
  output O_4
);

  wire multiplexer_1_out, multiplexer_2_out, multiplexer_3_out, multiplexer_4_out;

  D_FF d_ff_1 (.D(multiplexer_1_out), .C(clk), .Q(O_1));  // open: nQ
  Multiplexer #(.Selector_Bits(2)) multiplexer_1 (
    .sel(\Sél ), .in_0(O_1), .in_1(G), .in_2(O_2), .in_3(I_1), .out(multiplexer_1_out));
  Multiplexer #(.Selector_Bits(2)) multiplexer_2 (
    .sel(\Sél ), .in_0(O_2), .in_1(O_1), .in_2(O_3), .in_3(I_2), .out(multiplexer_2_out));
  D_FF d_ff_2 (.D(multiplexer_2_out), .C(clk), .Q(O_2));  // open: nQ
  D_FF d_ff_3 (.D(multiplexer_3_out), .C(clk), .Q(O_3));  // open: nQ
  Multiplexer #(.Selector_Bits(2)) multiplexer_3 (
    .sel(\Sél ), .in_0(O_3), .in_1(O_2), .in_2(O_4), .in_3(I_3), .out(multiplexer_3_out));
  Multiplexer #(.Selector_Bits(2)) multiplexer_4 (
    .sel(\Sél ), .in_0(O_4), .in_1(O_3), .in_2(D), .in_3(I_4), .out(multiplexer_4_out));
  D_FF d_ff_4 (.D(multiplexer_4_out), .C(clk), .Q(O_4));  // open: nQ
endmodule
